# Fritzing sketch Receiver Scheme (saved by Fritzing 0.9.2b)
breadboards: 1

parts:
  Q1 = NPN-Transistor [package="TO92 [THT]"]
  Q2 = NPN-Transistor [package="TO92 [THT]"]
  Q3 = NPN-Transistor [package="TO92 [THT]"]
  Q4 = NPN-Transistor [package="TO92 [THT]"]
  Componente1 = Arduino Nano (Rev3.0)
  R1 = Resistor [tolerance=±5% resistance=1k package=THT]
  R2 = Resistor [tolerance=±5% resistance=1k package=THT]
  R3 = Resistor [tolerance=±5% resistance=1k package=THT]
  M1 = DC Motor
  Q5 = NPN-Transistor [package="TO92 [THT]"]
  Q6 = NPN-Transistor [package="TO92 [THT]"]
  Q7 = NPN-Transistor [package="TO92 [THT]"]
  Q8 = NPN-Transistor [package="TO92 [THT]"]
  R4 = Resistor [tolerance=±5% resistance=1k package=THT]
  R5 = Resistor [tolerance=±5% resistance=1k package=THT]
  part = Resistor [tolerance=±5% resistance=1k package=THT]
  M2 = DC Motor
  R7 = Resistor [tolerance=±0.05% resistance=1k package=THT]
  R8 = Resistor [tolerance=±5% resistance=1k package=THT]
  VCC1 = Battery block 9V
  U1 = Voltage Regulator [package=to-92]

nets:
  N1: Q1.E, Q2.C, Q5.E, Q6.C, U1.OUT
  N2: Q1.B, R7.Pin_0
  N3: Q1.C, Q3.C, M1.pin_2
  N4: Q2.E, Q4.E, M1.pin_1
  N5: Q2.B, R3.Pin_0
  GND: Q3.E, Q4.C, Componente1.GND, Q7.E, Q8.C, VCC1.-, U1.GND
  N6: Q3.B, R2.Pin_0
  N7: Q4.B, R1.Pin_0
  N8: Componente1.D2, R5.Pin_1, R8.Pin_1
  N9: Componente1.D3, R4.Pin_1, part.Pin_1
  N10: Componente1.D4, R2.Pin_1, R3.Pin_1
  N11: Componente1.D5, R1.Pin_1, R7.Pin_1
  N12: Q5.B, R8.Pin_0
  N13: Q5.C, Q7.C, M2.pin_2
  N14: Q6.E, Q8.E, M2.pin_1
  N15: Q6.B, R4.Pin_0
  N16: Q7.B, part.Pin_0
  N17: Q8.B, R5.Pin_0
  N18: VCC1.+, U1.IN
